# Fritzing sketch sailboatSchematics (saved by Fritzing 0.9.3b)
breadboards: 1

parts:
  ArduinoMega = Arduino Mega 2560 (Rev3)
  GPS_EM506_pins = EM408_CON [package=em408_con]
  Compass_HMC6352 = Compass Module - HMC6352
  SD_card = MicroSD Card Module
  9DOF_IMU = 9 Degrees of Freedom - Sensor Stick
  Arduino's_lipo_batery = LIPO-2000mAh [package=lipo-2000]
  Servo's_Lipo_battery = Battery Holders [package=lipo-1100mAh]
  Rudder_Servo = Basic Servo
  Sail_Servo = Basic Servo
  10k_resistor_2 = Resistor [tolerance=±5% resistance=10k package=THT]
  Anemometer = Momentary Switch [package=ksa_sealed_tac_switch]
  10k_resistor_1 = Resistor [tolerance=±5% resistance=10k package=THT]
  bidirectional_signal_converter = Logic Level Converter

nets:
  N1: ArduinoMega.D21/SCL, Compass_HMC6352.SCL
  N2: ArduinoMega.D20/SDA, Compass_HMC6352.SDA
  N3: ArduinoMega.D19/RX1, bidirectional_signal_converter.TX_LV
  N4: ArduinoMega.D18/TX1, bidirectional_signal_converter.RX_LV
  N5: ArduinoMega.D17_PWM/RX2, 9DOF_IMU.SDA
  N6: ArduinoMega.D16_PWM/TX2, 9DOF_IMU.SCL
  N7: ArduinoMega.D15/RX3, GPS_EM506_pins.RX
  N8: ArduinoMega.D9_PWM, Rudder_Servo.pulse
  N9: ArduinoMega.D8_PWM, Sail_Servo.pulse
  VCC: ArduinoMega.3V3, Compass_HMC6352.VCC, SD_card.VCC, bidirectional_signal_converter.LV
  VCC_2: ArduinoMega.5V, GPS_EM506_pins.VCC, 9DOF_IMU.VCC, 10k_resistor_2.Pin_0, Anemometer.2, Anemometer.4, bidirectional_signal_converter.HV
  GND: ArduinoMega.GND, GPS_EM506_pins.GND, Compass_HMC6352.GND, SD_card.GND, 9DOF_IMU.GND, Arduino's_lipo_batery.-, Servo's_Lipo_battery.-, Rudder_Servo.gnd, Sail_Servo.gnd, 10k_resistor_1.Pin_0, bidirectional_signal_converter.GND
  N10: ArduinoMega.VIN, Arduino's_lipo_batery.+
  N11: ArduinoMega.D2_PWM, Anemometer.1, Anemometer.3, 10k_resistor_1.Pin_1
  N12: SD_card.MISO, bidirectional_signal_converter.RX_HV
  N13: SD_card.MOSI, bidirectional_signal_converter.TX_HV
  VCC_3: Servo's_Lipo_battery.+, Rudder_Servo.vcc, Sail_Servo.vcc

notes:
  9DOF will use UART serial ports. lets supose sda is tx and scl is rx (so we can use this part)
  COMPASS HMC6352
  GPS EM506
  Rudder Servo
  Sail Servo
  RED - 5v >
  ORANGE - 3.3v
  BLACK - gnd
  YELLOW - digital signal
  GREEN - analog signal
  BLUE - SDA
  PINK - SDL
  GREY - arduino's RX
  CYAN - arduino's TX
  Wind vane ground (blk) and signal (green) pins
  Anemometer
